# Fritzing sketch gps_sim800_tracker (saved by Fritzing 0.9.3b)
circuit board: 2.5cm x 6cm
breadboards: 1

parts:
  J1 = female pin header, 5 pins [form="♀ (female)"]
  J2 = female pin header, 6 pins [form="♀ (female)"]  # not connected
  GPS = female pin header, 4 pins [form="♀ (female)"]
  U1 = MCP73831 [package=sot23-5]
  S1 = SPST Switch [package=switch-spdt]
  usb = USB Connectors [package=usb-microb]
  bat_- = female pin header, 1 pin [form="♀ (female)"]
  bat+ = female pin header, 1 pin [form="♀ (female)"]
  R1 = Resistor [tolerance=±5% resistance=2k package="0805 [SMD]"]
  R2 = Resistor [tolerance=±5% resistance=470 package="0805 [SMD]"]
  LED2 = smd LED [color="Red (633nm)" package="0805 [SMD]"]
  R3 = Resistor [tolerance=±5% resistance=470 package="0805 [SMD]"]
  LED1 = smd LED [color="Red (633nm)" package="0805 [SMD]"]
  C2 = Ceramic Capacitor [capacitance=4.7µF package="1206 [SMD, multilayer]"]
  C1 = Ceramic Capacitor [capacitance=4.7µF package="1206 [SMD, multilayer]"]
  Part1 = Arduino Pro Mini v13

nets:
  3.3V: J1.pin1, GPS.pin4, S1.O, Part1.RAW
  N1: J1.pin3, Part1.D11_PWM/MOSI
  N2: J1.pin4, Part1.D10_PWM/SS
  GND: J1.pin5, GPS.pin1, U1.VSS, usb.GND, bat_-.pin1, R1.Pin_1, R3.Pin_0, C2.0, C1.1, Part1.GND
  N3: GPS.pin2, Part1.D8
  N4: GPS.pin3, Part1.D9_PWM
  N5: U1.STAT, R2.Pin_1
  N6: U1.VBAT, S1.P, bat+.pin1, C1.0
  N7: U1.VIN, usb.VBUS, LED2.anode, C2.1
  N8: U1.PROG, R1.Pin_0
  N9: R2.Pin_0, LED2.cathode
  N10: R3.Pin_1, LED1.cathode
  N11: LED1.anode, Part1.D13/SCK
